// Logisim project third.circ as structural Verilog
module main (
  input  [31:0] a,
  input  [31:0] b,
  input  [3:0] aluop,
  input  output_inverted,
  input  output_inc,
  input  clk,
  input  rst,
  output [31:0] res_low,
  output [31:0] res_high
);

  wire adder_2_cout, done;
  wire [0:0] ADD_HIGH;
  wire [31:0] ADD_LOW, adder_1_out, adder_2_out, multiplexer_1_out, multiplexer_2_out, multiplexer_3_out,
       multiplexer_4_out, not_1_out, not_2_out;

  D_Flip_Flop u_done (.Q(done), .preset(1'b1), .reset(1'b1));  // open: D, clk, Qn
  CSA csa_1 (.a(a), .b(b), .s(ADD_LOW), .cout(ADD_HIGH[0]));  // open: cin
  Multiplexer #(.select(4), .width(32)) multiplexer_1 (
    .in0(ADD_LOW), .out(multiplexer_1_out), .sel(aluop));  // open: in1, in2, in3, in4, in5, in6, in7, in8, in9, in10, in11, in12, in13, in14, in15
  Multiplexer #(.select(4), .width(32)) multiplexer_2 (
    .in0({{31{1'b0}}, ADD_HIGH[0]}), .out(multiplexer_2_out), .sel(aluop));  // open: in1, in2, in3, in4, in5, in6, in7, in8, in9, in10, in11, in12, in13, in14, in15
  assign not_1_out = ~multiplexer_1_out;  // NOT_Gate not_1, 32 bits wide
  Multiplexer #(.width(32)) multiplexer_3 (
    .in0(multiplexer_2_out), .in1(not_2_out), .out(multiplexer_3_out), .sel(output_inverted));
  assign not_2_out = ~multiplexer_2_out;  // NOT_Gate not_2, 32 bits wide
  Multiplexer #(.width(32)) multiplexer_4 (
    .in0(multiplexer_1_out), .in1(not_1_out), .out(multiplexer_4_out), .sel(output_inverted));
  Adder #(.width(32)) adder_1 (
    .a(multiplexer_3_out), .b({32{1'b0}}), .out(adder_1_out), .cin(adder_2_cout));  // open: cout
  Adder #(.width(32)) adder_2 (.a(multiplexer_4_out), .b(32'h1), .out(adder_2_out), .cout(adder_2_cout));  // open: cin
  Multiplexer #(.width(32)) multiplexer_5 (
    .in0(multiplexer_3_out), .in1(adder_1_out), .out(res_high), .sel(output_inc));
  Multiplexer #(.width(32)) multiplexer_6 (.in0(multiplexer_4_out), .in1(adder_2_out), .out(res_low), .sel(output_inc));

  // Other names for the same wires on the sheet: inc = output_inc; invert = output_inverted
endmodule

module counter2 (
  input  clk,
  input  reset,
  output num
);

  wire adder_1_out;

  Adder #(.width(1)) adder_1 (.a(num), .b(1'b1), .out(adder_1_out));  // open: cin, cout
  Register #(.width(1)) register_1 (.D(adder_1_out), .clk(clk), .Q(num), .clr(reset));  // open: en
endmodule

module Div (
  input  start,
  input  clk,
  input  [31:0] dividend,
  input  [31:0] divisor,
  output done,
  output [31:0] remainder,
  output [31:0] quotient
);

  wire comparator_1_gt, comparator_2_lt, counter2_1_num, not_1_out, not_3_out, undriven;
  wire [7:0] adder_1_out, counter_q;
  wire [31:0] adder_2_out, multiplexer_1_out, multiplexer_2_out, multiplexer_3_out, multiplexer_4_out,
       multiplexer_5_out, shifter_1_out, shifter_1_out_2, subtractor_1_out;
  wire [63:0] q_q;

  not not_1 (not_1_out, counter2_1_num);
  Multiplexer #(.width(32)) multiplexer_1 (
    .in0(q_q[31:0]), .in1(adder_2_out), .out(multiplexer_1_out), .sel(not_3_out));
  Adder adder_1 (.a(counter_q), .b(8'h1), .out(adder_1_out));  // open: cin, cout
  Register counter (.D(adder_1_out), .en(not_1_out), .clk(clk), .Q(counter_q), .clr(start));
  Multiplexer #(.width(32)) multiplexer_2 (
    .in0(shifter_1_out_2), .in1(multiplexer_3_out), .out(multiplexer_2_out), .sel(counter2_1_num));
  Multiplexer #(.width(32)) multiplexer_3 (
    .in0(q_q[63:32]), .in1(subtractor_1_out), .out(multiplexer_3_out), .sel(not_3_out));
  Multiplexer #(.width(32)) multiplexer_4 (
    .in0(shifter_1_out), .in1(multiplexer_1_out), .out(multiplexer_4_out), .sel(counter2_1_num));
  Multiplexer #(.width(32)) multiplexer_5 (
    .in0(multiplexer_4_out), .in1(dividend), .out(multiplexer_5_out), .sel(start));
  Register #(.width(32)) a (.D(multiplexer_2_out), .en(done), .clk(clk), .Q(q_q[63:32]), .clr(start));
  Register #(.width(32)) q (.D(multiplexer_5_out), .en(done), .clk(clk), .Q(q_q[31:0]), .clr(undriven));
  counter2 counter2_1 (.clk(clk), .reset(start), .num(counter2_1_num));
  Comparator comparator_1 (.a(counter_q), .b(8'h20), .gt(comparator_1_gt));  // open: eq, lt
  Comparator #(.width(32)) comparator_2 (.a(q_q[63:32]), .b(divisor), .lt(comparator_2_lt));  // open: gt, eq
  not not_2 (done, comparator_1_gt);
  Shifter #(.width(64)) shifter_1 (.in(q_q), .\dist (6'b000001), .out({shifter_1_out_2, shifter_1_out}));
  not not_3 (not_3_out, comparator_2_lt);
  Register #(.width(32)) register_1 (.D(q_q[63:32]), .en(done), .clk(clk), .Q(remainder));  // open: clr
  Subtractor #(.width(32)) subtractor_1 (.a(q_q[63:32]), .b(divisor), .out(subtractor_1_out));  // open: bin, bout
  Adder #(.width(32)) adder_2 (.a(q_q[31:0]), .b(32'h1), .out(adder_2_out));  // open: cin, cout
  Register #(.width(32)) register_2 (.D(q_q[31:0]), .en(done), .clk(clk), .Q(quotient));  // open: clr
endmodule

module CSA (
  input  cin,
  input  [31:0] a,
  input  [31:0] b,
  output [31:0] s,
  output cout
);

  wire adder_1_cout, adder_2_cout, adder_3_cout, adder_4_cout, adder_5_cout, adder_6_cout, adder_7_cout,
       multiplexer_2_out, multiplexer_3_out;
  wire [7:0] adder_2_out, adder_3_out, adder_4_out, adder_5_out, adder_6_out, adder_7_out;

  Adder adder_1 (.a(a[7:0]), .b(b[7:0]), .out(s[7:0]), .cin(cin), .cout(adder_1_cout));
  Adder adder_2 (.a(a[15:8]), .b(b[15:8]), .out(adder_2_out), .cout(adder_2_cout));  // open: cin
  Adder adder_3 (.a(a[15:8]), .b(b[15:8]), .out(adder_3_out), .cin(1'b1), .cout(adder_3_cout));
  Adder adder_4 (.a(a[23:16]), .b(b[23:16]), .out(adder_4_out), .cout(adder_4_cout));  // open: cin
  Adder adder_5 (.a(a[23:16]), .b(b[23:16]), .out(adder_5_out), .cin(1'b1), .cout(adder_5_cout));
  Adder adder_6 (.a(a[31:24]), .b(b[31:24]), .out(adder_6_out), .cout(adder_6_cout));  // open: cin
  Adder adder_7 (.a(a[31:24]), .b(b[31:24]), .out(adder_7_out), .cin(1'b1), .cout(adder_7_cout));
  Multiplexer #(.width(8)) multiplexer_1 (.in0(adder_2_out), .in1(adder_3_out), .out(s[15:8]), .sel(adder_1_cout));
  Multiplexer multiplexer_2 (.in0(adder_2_cout), .in1(adder_3_cout), .out(multiplexer_2_out), .sel(adder_1_cout));
  Multiplexer multiplexer_3 (.in0(adder_4_cout), .in1(adder_5_cout), .out(multiplexer_3_out), .sel(multiplexer_2_out));
  Multiplexer #(.width(8)) multiplexer_4 (
    .in0(adder_6_out), .in1(adder_7_out), .out(s[31:24]), .sel(multiplexer_3_out));
  Multiplexer multiplexer_5 (.in0(adder_6_cout), .in1(adder_7_cout), .out(cout), .sel(multiplexer_3_out));
  Multiplexer #(.width(8)) multiplexer_6 (
    .in0(adder_4_out), .in1(adder_5_out), .out(s[23:16]), .sel(multiplexer_2_out));
endmodule

module CsaveA (
  input  cin,
  input  [31:0] a,
  input  [31:0] b,
  input  [31:0] c,
  output [31:0] s,
  output cout
);

  wire [31:0] parallel_fulladders_1_cout, parallel_fulladders_1_s, shifter_1_out;

  Parallel_FullAdders parallel_fulladders_1 (
    .a(a), .b(b), .cin(c), .s(parallel_fulladders_1_s), .cout(parallel_fulladders_1_cout));
  Shifter #(.width(32)) shifter_1 (.in(parallel_fulladders_1_cout), .\dist (5'b00001), .out(shifter_1_out));
  CSA csa_1 (.cin(cin), .a(parallel_fulladders_1_s), .b(shifter_1_out), .s(s), .cout(cout));
endmodule

module Parallel_FullAdders (
  input  [31:0] a,
  input  [31:0] b,
  input  [31:0] cin,
  output [31:0] s,
  output [31:0] cout
);

  wire [31:0] and_1_out, and_2_out, xor_1_out;

  assign and_1_out = a & b;  // AND_Gate and_1, 32 bits wide
  assign xor_1_out = a ^ b;  // XOR_Gate xor_1, 32 bits wide
  assign and_2_out = xor_1_out & cin;  // AND_Gate and_2, 32 bits wide
  assign s = xor_1_out ^ cin;  // XOR_Gate xor_2, 32 bits wide
  assign cout = and_2_out | and_1_out;  // OR_Gate or_1, 32 bits wide
endmodule

module mul (
  input  clk,
  input  start,
  input  [31:0] a,
  input  [31:0] b,
  output done,
  output [63:0] Result
);

  wire and_1_out, comparator_1_gt, comparator_1_lt, CSA_cout, Init, nor_1_out, not_1_out, not_2_out,
       Opperation, or_1_out, or_2_out, or_3_out, or_4_out, OR_R1_FLAG, RE_q, RE_signal, signal_1, signal_2,
       undriven;
  wire [31:0] CSA2_s, CSA_s, multiplexer_1_out, multiplexer_2_out, multiplexer_3_out, multiplexer_4_out,
       multiplexer_5_out, R1_q, R2_q, R2_q_2, shifter_1_out, shifter_3_out;
  wire [63:0] multiplexer_6_out, multiplexer_7_out, shifter_2_out, shifter_4_out;

  not not_1 (not_1_out, OR_R1_FLAG);
  Multiplexer #(.width(32)) multiplexer_1 (
    .in0({32{1'b0}}), .in1(shifter_2_out[31:0]), .out(multiplexer_1_out), .sel(shifter_1_out[0]));
  Multiplexer #(.width(32)) multiplexer_2 (.in0({32{1'b0}}), .in1(R2_q_2), .out(multiplexer_2_out), .sel(R1_q[0]));
  Multiplexer #(.width(32)) multiplexer_3 (
    .in0({32{1'b0}}), .in1(shifter_2_out[63:32]), .out(multiplexer_3_out), .sel(shifter_1_out[0]));
  nor nor_1 (nor_1_out, Opperation, start);
  and and_1 (and_1_out, not_1_out, Opperation);
  Multiplexer #(.width(32)) multiplexer_4 (.in0({32{1'b0}}), .in1(R2_q), .out(multiplexer_4_out), .sel(R1_q[0]));
  and and_2 (signal_1, Init, start);
  Shifter #(.shift("lr"), .width(32)) shifter_1 (.in(R1_q), .\dist (5'b00001), .out(shifter_1_out));
  or or_1 (or_1_out, nor_1_out, and_1_out);
  and and_3 (signal_2, OR_R1_FLAG, Opperation);
  D_Flip_Flop u_Init (.D(or_1_out), .clk(clk), .Q(Init), .preset(start));  // open: Qn, reset
  D_Flip_Flop u_Opperation (.D(or_2_out), .clk(clk), .Q(Opperation), .reset(undriven));  // open: Qn, preset
  or or_2 (or_2_out, signal_1, signal_2);
  Shifter #(.width(64)) shifter_2 (.in({R2_q_2, R2_q}), .\dist (6'b000001), .out(shifter_2_out));
  CsaveA CSA (.a(multiplexer_4_out), .b(multiplexer_1_out), .c(Result[31:0]), .s(CSA_s), .cout(CSA_cout));  // open: cin
  CsaveA CSA2 (
    .cin(CSA_cout), .a(multiplexer_2_out), .b(multiplexer_3_out), .c(Result[63:32]), .s(CSA2_s));  // open: cout
  Shifter #(.shift("lr"), .width(32)) shifter_3 (.in(shifter_1_out), .\dist (5'b00001), .out(shifter_3_out));
  Shifter #(.width(64)) shifter_4 (.in(shifter_2_out), .\dist (6'b000001), .out(shifter_4_out));
  and and_4 (RE_signal, Opperation, not_2_out);
  not not_2 (not_2_out, OR_R1_FLAG);
  Multiplexer #(.width(32)) multiplexer_5 (.in0(shifter_3_out), .in1(a), .out(multiplexer_5_out), .sel(signal_1));
  or or_3 (or_3_out, signal_1, signal_2);
  Multiplexer #(.width(64)) multiplexer_6 (
    .in0({{32{1'b0}}, b}), .in1(shifter_4_out), .out(multiplexer_6_out), .sel(signal_2));
  or or_4 (or_4_out, RE_signal, signal_1);
  Multiplexer #(.width(64)) multiplexer_7 (
    .in0({64{1'b0}}), .in1({CSA2_s, CSA_s}), .out(multiplexer_7_out), .sel(signal_2));
  Register #(.width(32)) R1 (.D(multiplexer_5_out), .en(or_3_out), .clk(clk), .Q(R1_q));  // open: clr
  Register #(.width(64)) R2 (.D(multiplexer_6_out), .en(or_3_out), .clk(clk), .Q({R2_q_2, R2_q}));  // open: clr
  Register #(.width(64)) R3 (.D(multiplexer_7_out), .en(or_3_out), .clk(clk), .Q(Result));  // open: clr
  Register #(.width(1)) RE (.D(RE_signal), .en(or_4_out), .clk(clk), .Q(RE_q));  // open: clr
  or or_5 (done, RE_q, RE_signal);
  Comparator #(.width(32)) comparator_1 (
    .a(R1_q), .b({32{1'b0}}), .gt(comparator_1_gt), .lt(comparator_1_lt));  // open: eq
  or or_6 (OR_R1_FLAG, comparator_1_gt, comparator_1_lt);

  // Other names for the same wires on the sheet: IN2[31:0] = b; IN1[31:0] = a; S = start
endmodule
